// Logisim project CSE231_Project.circ as structural Verilog: 2 circuits, main circuit main
module main (
  input  x,
  input  E,
  input  Clear,
  input  Forward,
  input  Left,
  input  Right,
  input  Stall,
  input  A,
  input  B,
  input  C,
  output Stall_2,
  output R2,
  output Left_2,
  output R1,
  output Right_2,
  output Forward_2
);

  wire and_1_out, and_2_out, and_3_out, and_4_out, and_5_out, and_6_out, and_7_out, and_8_out, and_9_out,
       and_10_out, and_12_out, and_15_out, clock_1_out, d_ff_1_q, d_ff_2_q, d_ff_3_q, not_1_out, not_2_out,
       not_3_out, not_4_out, not_5_out, not_6_out, not_7_out, not_8_out, not_9_out, or_1_out, or_2_out,
       or_3_out, or_4_out, or_5_out;

  not not_1 (not_1_out, Left);
  and and_1 (and_1_out, not_1_out, Right);
  or or_1 (or_1_out, Forward, and_1_out);
  or or_2 (or_2_out, Forward, Left);
  not not_2 (not_2_out, x);
  not not_3 (not_3_out, d_ff_1_q);
  not not_4 (not_4_out, d_ff_2_q);
  not not_5 (not_5_out, d_ff_3_q);
  and and_2 (and_2_out, d_ff_1_q, d_ff_2_q, x);
  and and_3 (and_3_out, or_1_out, not_2_out);
  and and_4 (and_4_out, d_ff_2_q, d_ff_3_q, x);
  not not_6 (not_6_out, d_ff_2_q);
  and and_5 (and_5_out, not_3_out, not_6_out, x);
  and and_6 (and_6_out, d_ff_3_q, x);
  and and_7 (and_7_out, not_2_out, or_2_out);
  and and_8 (and_8_out, not_4_out, x);
  and and_9 (and_9_out, or_1_out, not_2_out);
  and and_10 (and_10_out, d_ff_1_q, not_5_out, x);
  or or_3 (or_3_out, and_3_out, and_4_out, and_2_out, and_5_out);
  or or_4 (or_4_out, and_6_out, and_7_out, and_8_out, and_9_out);
  or or_5 (or_5_out, and_7_out, and_10_out);
  Clock clock_1 (.out(clock_1_out));
  D_Flip_Flop d_ff_1 (
    .clk(clock_1_out), .D(or_3_out), .Q(d_ff_1_q), .preset(A), .en(Clear), .reset(Clear));  // open: Qn
  D_Flip_Flop d_ff_2 (
    .clk(clock_1_out), .D(or_4_out), .Q(d_ff_2_q), .preset(B), .en(Clear), .reset(Clear));  // open: Qn
  D_Flip_Flop d_ff_3 (
    .clk(clock_1_out), .D(or_5_out), .Q(d_ff_3_q), .preset(C), .en(Clear), .reset(Clear));  // open: Qn
  not not_7 (not_7_out, d_ff_3_q);
  not not_8 (not_8_out, d_ff_1_q);
  not not_9 (not_9_out, d_ff_2_q);
  and and_11 (Stall_2, not_8_out, not_9_out, not_7_out);
  and and_12 (and_12_out, not_8_out, not_9_out, d_ff_3_q);
  and and_13 (R2, not_8_out, d_ff_2_q, not_7_out);
  and and_14 (Left_2, not_8_out, d_ff_2_q, d_ff_3_q);
  and and_15 (and_15_out, d_ff_1_q, not_9_out, not_7_out);
  and and_16 (R1, d_ff_1_q, not_9_out, d_ff_3_q);
  and and_17 (Right_2, d_ff_1_q, d_ff_2_q, not_7_out);
  and and_18 (Forward_2, d_ff_1_q, d_ff_2_q, d_ff_3_q);

  assign E = Clear;

  // Notes on the sheet:
  //   D0
  //   D1
  //   CP
  //   A
  //   B
  //   C
endmodule

module CSE231_Project (
  input  Obstacle__x,
  input  E,
  input  Clear,
  input  Forward,
  input  Left,
  input  Right,
  input  Break,
  input  A,
  input  B,
  input  C,
  output Stall,
  output R2,
  output Left_2,
  output R1,
  output Right_2,
  output Forward_2
);

  main main_1 (
    .Forward(Forward), .Left(Left), .Right(Right), .Stall(Break), .x(Obstacle__x), .E(E), .Clear(Clear),
    .A(A), .B(B), .C(C), .Stall_2(Stall), .R2(R2), .Left_2(Left_2), .R1(R1), .Right_2(Right_2),
    .Forward_2(Forward_2));

  // Notes on the sheet:
  //   Initial State
  //   Regulation:
  //   At first Enable the rover
  //   Simulate -> Ticks Enabled
  //   Off the previous switch after pressing new
endmodule
