// Logisim project Pattern LOCK Project.circ as structural Verilog: 3 circuits, main circuit Main
module Main (
  input  _0,
  input  _1,
  input  _2,
  input  _3,
  input  _4,
  input  _5,
  input  _6,
  input  _7,
  input  _8
);

  wire CLOCK_out, Decimal_to_Binary_Converter_a, Decimal_to_Binary_Converter_b,
       Decimal_to_Binary_Converter_c, Decimal_to_Binary_Converter_d, Pattern_y, RESET_out;

  Button CLOCK (.out(CLOCK_out));
  Decimal_to_Binary Decimal_to_Binary_Converter (
    ._0(_0), ._1(_1), ._2(_2), ._3(_3), ._4(_4), ._5(_5), ._6(_6), ._7(_7), ._8(_8),
    .a(Decimal_to_Binary_Converter_a), .b(Decimal_to_Binary_Converter_b), .c(Decimal_to_Binary_Converter_c),
    .d(Decimal_to_Binary_Converter_d));
  Pattern Pattern (
    .y(Pattern_y), .a(Decimal_to_Binary_Converter_a), .b(Decimal_to_Binary_Converter_b),
    .c(Decimal_to_Binary_Converter_c), .d(Decimal_to_Binary_Converter_d), .Ck(CLOCK_out), .RESET(RESET_out));
  Button RESET (.out(RESET_out));
  LED Output (.in(Pattern_y));

  // Notes on the sheet:
  //   pattern: 046785
endmodule

module Pattern (
  input  a,
  input  b,
  input  c,
  input  d,
  input  Ck,
  input  RESET,
  output y
);

  wire and_1_out, and_2_out, and_3_out, and_4_out, and_5_out, and_6_out, and_7_out, d_ff_1_qn, d_ff_2_qn,
       d_ff_3_qn, d_ff_4_qn, or_1_out, or_2_out;

  and and_1 (and_1_out, d_ff_1_qn, b, c, d);
  and and_2 (and_2_out, d_ff_2_qn, d_ff_3_qn, d_ff_4_qn);
  and and_3 (and_3_out, d_ff_1_qn, b, d_ff_4_qn);
  and and_4 (and_4_out, d_ff_1_qn, b, d_ff_4_qn);
  and and_5 (and_5_out, d_ff_1_qn, c, d_ff_4_qn);
  and and_6 (and_6_out, d_ff_1_qn, b, d_ff_3_qn, d);
  and and_7 (and_7_out, a, d_ff_2_qn, d_ff_3_qn, d_ff_4_qn);
  and and_8 (y, d_ff_1_qn, b, d_ff_3_qn, d);
  or or_1 (or_1_out, and_2_out, and_3_out);
  or or_2 (or_2_out, and_5_out, and_6_out, and_7_out);
  D_Flip_Flop d_ff_1 (.clk(Ck), .D(and_1_out), .Q(a), .Qn(d_ff_1_qn), .reset(RESET));  // open: preset, en
  D_Flip_Flop d_ff_2 (.clk(Ck), .D(or_1_out), .Q(b), .Qn(d_ff_2_qn), .reset(RESET));  // open: preset, en
  D_Flip_Flop d_ff_3 (.clk(Ck), .D(and_4_out), .Q(c), .Qn(d_ff_3_qn), .reset(RESET));  // open: preset, en
  D_Flip_Flop d_ff_4 (.clk(Ck), .D(or_2_out), .Q(d), .Qn(d_ff_4_qn), .reset(RESET));  // open: preset, en

  // Notes on the sheet:
  //   A'
  //   C'
  //   B'
  //   D'
endmodule

module Decimal_to_Binary (
  input  _0,
  input  _1,
  input  _2,
  input  _3,
  input  _4,
  input  _5,
  input  _6,
  input  _7,
  input  _8,
  output a,
  output b,
  output c,
  output d
);

  wire _9_out;

  Button _9 (.out(_9_out));
  or or_1 (a, _8, _9_out);
  or or_2 (c, _2, _3, _6, _7);
  or or_3 (b, _4, _5, _6, _7);
  or or_4 (d, _1, _9_out, _7, _5, _3);
endmodule
